# Fritzing sketch interrupt_switch_wiring (saved by Fritzing 0.9.2b)
breadboards: 1

parts:
  Part1 = Arduino Uno (Rev3)
  S1 = Pushbutton [package="[THT]"]
  LED1 = LED - 5mm [color="Red (633nm)" package="5 mm [THT]"]

nets:
  N1: Part1.D2, LED1.cathode
  N2: Part1.5V, S1.Pin_3, S1.Pin_4, LED1.anode
  N3: Part1.GND, S1.Pin_1, S1.Pin_2
